// Digital circuit ALU.dig as structural Verilog
module ALU (
  input  [15:0] A,
  input  [15:0] B,
  input  C_i,
  input  [3:0] Op
);

  wire undriven;

  // And and_1 has open pins: In_1=C_i, In_2=Op[3], out=open
  Add add_1 (.a(A[0]), .b(B[0]), .c_i(undriven));  // open: s, c_o
  Sub sub_1 (.a(A[0]), .b(B[0]), .c_i(undriven));  // open: s, c_o
  // And and_2 has open pins: In_1=A[0], In_2=B[0], out=open
  // Or or_1 has open pins: In_1=A[0], In_2=B[0], out=open
  // XOr xor_1 has open pins: In_1=A[0], In_2=B[0], out=open
  Mul mul_1 (.a(A[0]), .b(B[0]));  // open: mul
  // Pins of 1 and 16 bits meet at A
  // Pins of 1 and 16 bits meet at B
endmodule
