// Digital circuit main.dig as structural Verilog
module main (
  input  clk
);

  wire AI, alu_1_p2, AO, BI, BO, BRK, carry, CE, clk_t, EO, EQL, II, J, nand_1_out, nand_2_out, nclk, PO,
       RAMI, RAMO, reg_a_1_p5, ROMO, SU, zero;
  wire [10:0] ADDR;
  wire [15:0] DATA, IR, ramdualport_1_d;

  REG_INST reg_inst_1 (.ii(II), .clk(clk_t), .INST(IR));  // open: ARG, OP
  // PC pc_1: pin names not known; wires that end beside it: ADDR, CE, clk_t, J, PO, ADDR, carry
  EEPROM #(.AddrBits(11), .Bits(8)) ROM_A (.A(ADDR), .CS(1'b1), .WE(1'b0), .OE(1'b1), .D(IR[7:0]));
  EEPROM #(.AddrBits(11), .Bits(8)) ROM_B (.A(ADDR), .CS(1'b1), .WE(1'b0), .OE(1'b1), .D(IR[15:8]));
  assign DATA[0] = ROMO ? IR[0] : 1'bz;  // Driver driver_1
  uINST uinst_1 ();  // open: nclk, OP, ARG, carry, zero, DATA, ADDR, CE, J, PO, II, MEMDO, RAMDI, SU, EO, BI, AI, GFX, MC, EXT0, HLT, GFXI, MEMAO, CONST, EXT1, EXT2, RAMAI, table
  RAMDualPort #(.AddrBits(4), .Bits(16)) ramdualport_1 (
    .A(ADDR[3:0]), .Din(DATA), .str(RAMI), .C(clk_t), .ld(1'b1), .D(ramdualport_1_d));
  nand nand_1 (nand_1_out, BRK, BRK);
  assign DATA[0] = RAMO ? ramdualport_1_d[0] : 1'bz;  // Driver driver_2
  nand nand_2 (nand_2_out, nand_1_out, clk);
  nand nand_3 (clk_t, nand_2_out, nand_2_out);
  // REG_A reg_a_1: pin names not known; wires that end beside it: DATA, clk_t, AI, AO, reg_a_1_p5, DATA
  // ALU alu_1: pin names not known; wires that end beside it: reg_a_1_p5, alu_1_p2, SU, EO, DATA, carry, zero, EQL
  // REG_B reg_b_1: pin names not known; wires that end beside it: DATA, RAMI, clk_t, BI, BO, ROMO, alu_1_p2, II, DATA, PO, J, CE
  nand nand_4 (nclk, clk_t, clk_t);
  // Pins of 1 and 8 bits meet at IR[7:0]
  // Pins of 4 and 11 bits meet at ADDR
  // Pins of 1 and 16 bits meet at DATA
  // Pins of 1 and 16 bits meet at ramdualport_1_d

  // Notes on the sheet:
  //   clk: Hz: 5
endmodule
